// Logisim project BigASM.circ as structural Verilog
module BOARD_BIG_ASM (
  output out_1
);

  wire button_1_out, CLK, CLR, d_ff_1_q, not_1_out, Write, Write_ASCII;
  wire [6:0] ASCII;
  wire [7:0] counter_1_q;
  wire [23:0] Dir_INPUT, Dir_MEMORY;
  wire [31:0] INPUT, MEMORY_IN, MEMORY_OUT;

  Button button_1 (.out(button_1_out));
  Clock clock_1 (.out(CLK));
  D_Flip_Flop d_ff_1 (.clk(CLK), .D(1'b1), .Q(d_ff_1_q), .reset(button_1_out));  // open: Qn, preset, en
  D_Flip_Flop d_ff_2 (.clk(CLK), .D(d_ff_1_q), .Qn(CLR), .reset(button_1_out));  // open: Q, preset, en
  BIG_ASM big_asm_1 (
    .DATA_INPUT(INPUT), .MEMORY_IN(MEMORY_OUT), .CLK(CLK), .CLR(CLR), .DIR_INPUT(Dir_INPUT),
    .MEMORY_OUT(MEMORY_IN), .DIR_MEMORY(Dir_MEMORY), .Write_OUTPUT(Write), .ASCII(ASCII),
    .Write_ASCII(Write_ASCII), .END(out_1));
  MEMORY memory_1 (.DIR(Dir_MEMORY), .DATA_IN(MEMORY_IN), .WRITE(Write), .CLK(CLK), .CLR(CLR), .DATA_OUT(MEMORY_OUT));
  INPUT input_1 (.DIR(Dir_INPUT), .CLK(CLK), .DATA_OUT(INPUT));
  Counter counter_1 (.load(1'b0), .count(not_1_out), .Q(counter_1_q), .clk(CLK), .clr(CLR));  // open: D, carry
  not not_1 (not_1_out, out_1);
  // Probe on counter_1_q
  TTY #(.rows(32), .cols(60)) tty_1 (.data(ASCII), .clk(CLK), .we(Write_ASCII), .clr(CLR));

  // Other names for the same wires on the sheet: END = out_1

  // Notes on the sheet:
  //   COUNTER
  //   BOARD
endmodule

module INPUT (
  input  [23:0] DIR,
  input  CLK,
  output [31:0] DATA_OUT
);

  RAM #(.addrWidth(24), .dataWidth(32)) ram_1 (.addr(DIR), .data(DATA_OUT), .clk(CLK), .ld(1'b1));  // open: sel, clr
endmodule

module MEMORY (
  input  [23:0] DIR,
  input  [31:0] DATA_IN,
  input  WRITE,
  input  CLK,
  input  CLR,
  output [31:0] DATA_OUT
);

  wire not_1_out;

  not not_1 (not_1_out, WRITE);
  RAM #(.addrWidth(24), .dataWidth(32), .bus("separate")) ram_1 (
    .addr(DIR), .din(DATA_IN), .data(DATA_OUT), .clk(CLK), .ld(not_1_out), .clr(CLR));  // open: str, sel
endmodule

module BIG_ASM (
  input  [31:0] DATA_INPUT,
  input  [31:0] MEMORY_IN,
  input  CLK,
  input  CLR,
  output [23:0] DIR_INPUT,
  output [31:0] MEMORY_OUT,
  output [23:0] DIR_MEMORY,
  output Write_OUTPUT,
  output [6:0] ASCII,
  output Write_ASCII,
  output END
);
endmodule

module PRINT_UDEC (
  input  [31:0] num,
  input  start,
  input  CLK,
  input  RST,
  output [6:0] ASCII,
  output Write_ASCII,
  output \end 
);

  wire _0_c, _0_n, demultiplexer_1_out0, demultiplexer_2_out0, demultiplexer_2_out1, demultiplexer_3_out0,
       demultiplexer_3_out1, IDLE_2_q, IDLE_3_q, IDLE_4_q, IDLE_q, Lc, Lc_0, Ln, Ln_0, or_1_out;
  wire [23:0] bit_extender_1_out;
  wire [31:0] c, c___1, c___1_t, divider_1_rem, memory_1_data_out, multiplexer_1_out, multiplexer_2_out,
       multiplexer_3_out, n, n___10, n___10___48;

  Multiplexer #(.width(32), .enable("false")) multiplexer_1 (
    .in0(num), .in1(n___10), .out(multiplexer_1_out), .sel(Lc_0));
  Divider #(.width(32)) divider_1 (.a(n), .b(32'ha), .out(n___10), .rem(divider_1_rem));  // open: upper
  Adder #(.width(32)) adder_1 (.a(divider_1_rem), .b(32'h30), .out(n___10___48));  // open: cin, cout
  or or_1 (or_1_out, demultiplexer_1_out0, \end );
  Register #(.width(32)) u_n (.D(multiplexer_1_out), .en(Ln), .Q(n), .clk(CLK), .clr(RST));
  D_Flip_Flop IDLE (.clk(CLK), .D(or_1_out), .Q(IDLE_q), .preset(RST));  // open: Qn, en, reset
  Demultiplexer #(.enable("false")) demultiplexer_1 (
    .out0(demultiplexer_1_out0), .out1(Ln_0), .in(IDLE_q), .sel(start));
  or or_2 (Write_ASCII, demultiplexer_3_out0, demultiplexer_2_out1);
  Multiplexer #(.width(32), .enable("false")) multiplexer_2 (
    .in0(c___1), .in1(c___1_t), .out(multiplexer_2_out), .sel(Write_ASCII));
  Adder #(.width(32)) adder_2 (.a(c), .b(32'h1), .out(c___1));  // open: cin, cout
  Subtractor #(.width(32)) subtractor_1 (.a(c), .b(32'h1), .out(c___1_t));  // open: bin, bout
  D_Flip_Flop IDLE_2 (.clk(CLK), .D(Ln_0), .Q(IDLE_2_q), .reset(RST));  // open: Qn, preset, en
  Register #(.width(32)) u_c (.D(multiplexer_2_out), .en(Lc), .Q(c), .clk(CLK), .clr(RST));
  or or_3 (Lc_0, IDLE_2_q, demultiplexer_3_out1);
  Multiplexer #(.width(32), .enable("false")) multiplexer_3 (
    .in0(c), .in1(c___1_t), .out(multiplexer_3_out), .sel(Write_ASCII));
  Comparator #(.width(32), .mode("unsigned")) comparator_1 (.a({32{1'b0}}), .b(n), .lt(_0_n));  // open: gt, eq
  Comparator #(.width(32), .mode("unsigned")) comparator_2 (.a({32{1'b0}}), .b(c), .lt(_0_c));  // open: gt, eq
  D_Flip_Flop IDLE_3 (.clk(CLK), .D(Write_ASCII), .Q(IDLE_3_q), .reset(RST));  // open: Qn, preset, en
  Demultiplexer #(.enable("false")) demultiplexer_2 (
    .out0(demultiplexer_2_out0), .out1(demultiplexer_2_out1), .in(IDLE_3_q), .sel(_0_c));
  Bit_Extender #(.in_width(32), .out_width(24)) bit_extender_1 (.in(multiplexer_3_out), .out(bit_extender_1_out));
  D_Flip_Flop IDLE_4 (.clk(CLK), .D(Lc_0), .Q(IDLE_4_q), .reset(RST));  // open: Qn, preset, en
  or or_4 (Lc, Lc_0, Write_ASCII);
  or or_5 (Ln, Ln_0, Lc_0);
  Demultiplexer #(.enable("false")) demultiplexer_3 (
    .out0(demultiplexer_3_out0), .out1(demultiplexer_3_out1), .in(IDLE_4_q), .sel(_0_n));
  D_Flip_Flop IDLE_5 (.clk(CLK), .D(demultiplexer_2_out0), .Q(\end ), .reset(RST));  // open: Qn, preset, en
  MEMORY memory_1 (
    .DIR(bit_extender_1_out), .DATA_IN(n___10___48), .WRITE(Lc_0), .CLK(CLK), .CLR(RST),
    .DATA_OUT(memory_1_data_out));
  Bit_Extender #(.in_width(32), .out_width(7)) bit_extender_2 (.in(memory_1_data_out), .out(ASCII));

  // Other names for the same wires on the sheet: Lc_1 = Write_ASCII; Sc = Write_ASCII; Ln_1 = Lc_0; Sn = Lc_0;
  //   Write = Lc_0
endmodule

module PRINT_DEC (
  input  [31:0] num,
  input  start,
  input  CLK,
  input  RST,
  output [6:0] ASCII,
  output Write_ASCII,
  output END
);

  wire demultiplexer_1_out0, demultiplexer_1_out1, demultiplexer_2_out0, demultiplexer_3_out0, end_t,
       IDLE_3_q, IDLE_q, or_1_out, or_2_out, or_3_out, S_ASCII, startUDEC, Write_ASCII_1;
  wire [6:0] ASCII_t;
  wire [31:0] multiplexer_1_out, negator_1_out;

  or or_1 (or_1_out, demultiplexer_1_out0, END);
  Negator #(.width(32)) negator_1 (.in(num), .out(negator_1_out));
  D_Flip_Flop IDLE (.clk(CLK), .D(or_1_out), .Q(IDLE_q), .preset(RST));  // open: Qn, en, reset
  Demultiplexer #(.enable("false")) demultiplexer_1 (
    .out0(demultiplexer_1_out0), .out1(demultiplexer_1_out1), .in(IDLE_q), .sel(start));
  Multiplexer #(.width(32), .enable("false")) multiplexer_1 (
    .in0(num), .in1(negator_1_out), .out(multiplexer_1_out), .sel(num[31]));
  Demultiplexer #(.enable("false")) demultiplexer_2 (
    .out0(demultiplexer_2_out0), .out1(S_ASCII), .in(demultiplexer_1_out1), .sel(num[31]));
  or or_2 (or_2_out, demultiplexer_2_out0, S_ASCII);
  D_Flip_Flop IDLE_2 (.clk(CLK), .D(or_2_out), .Q(startUDEC), .reset(RST));  // open: Qn, preset, en
  PRINT_UDEC print_udec_1 (
    .num(multiplexer_1_out), .start(startUDEC), .CLK(CLK), .RST(RST), .ASCII(ASCII_t),
    .Write_ASCII(Write_ASCII_1), .\end (end_t));
  D_Flip_Flop IDLE_3 (.clk(CLK), .D(or_3_out), .Q(IDLE_3_q), .reset(RST));  // open: Qn, preset, en
  or or_3 (or_3_out, startUDEC, demultiplexer_3_out0);
  Demultiplexer #(.enable("false")) demultiplexer_3 (
    .out0(demultiplexer_3_out0), .out1(END), .in(IDLE_3_q), .sel(end_t));
  Multiplexer #(.width(7), .enable("false")) multiplexer_2 (
    .in0(ASCII_t), .in1(7'b0101101), .out(ASCII), .sel(S_ASCII));
  or or_4 (Write_ASCII, S_ASCII, Write_ASCII_1);

  // Other names for the same wires on the sheet: sign = num[31]; Write_ASCII_0 = S_ASCII
endmodule

module TEST_PRINT (
  input  [31:0] in_1,
  output out_2
);

  wire button_1_out, button_2_out, CLK, CLR, d_ff_1_q, Write_ASCII;
  wire [6:0] ASCII;

  Button button_1 (.out(button_1_out));
  Clock clock_1 (.out(CLK));
  D_Flip_Flop d_ff_1 (.clk(CLK), .D(1'b1), .Q(d_ff_1_q), .reset(button_1_out));  // open: Qn, preset, en
  D_Flip_Flop d_ff_2 (.clk(CLK), .D(d_ff_1_q), .Qn(CLR), .reset(button_1_out));  // open: Q, preset, en
  Button button_2 (.out(button_2_out));
  PRINT_UDEC print_udec_1 ();  // open: num, start, CLK, RST, ASCII, Write_ASCII, end
  PRINT_DEC print_dec_1 (
    .num(in_1), .start(button_2_out), .CLK(CLK), .RST(CLR), .ASCII(ASCII), .Write_ASCII(Write_ASCII),
    .END(out_2));
  TTY #(.rows(32), .cols(60)) tty_1 (.data(ASCII), .clk(CLK), .we(Write_ASCII), .clr(CLR));
endmodule

module DATA_PATH__M (
  input  in_1,
  input  in_2,
  input  in_3,
  input  in_4,
  input  in_5,
  input  [31:0] in_6,
  input  [31:0] in_7,
  input  [31:0] in_8,
  output out_9,
  output out_10,
  output [31:0] out_11
);

  wire [31:0] I, I___1, L_A, L_I, multiplexer_1_out, multiplexer_2_out;

  Multiplexer #(.width(32), .enable("false")) multiplexer_1 (.in0(in_6), .in1(I), .out(multiplexer_1_out), .sel(in_5));
  Multiplexer #(.width(32), .enable("false")) multiplexer_2 (
    .in0(in_7), .in1(I___1), .out(multiplexer_2_out), .sel(in_2));
  Adder #(.width(32)) adder_1 (.a(I), .b(32'h1), .out(I___1));  // open: cin, cout
  Register #(.width(32)) register_1 (.D(multiplexer_1_out), .en(in_4), .Q(out_11), .clk(in_3));  // open: clr
  Register #(.width(32)) register_2 (.D(multiplexer_2_out), .en(in_1), .Q(I), .clk(in_3));  // open: clr
  INPUT input_1 (.DIR(I[23:0]), .CLK(in_3), .DATA_OUT(L_I));
  INPUT input_2 (.DIR(out_11[23:0]), .CLK(in_3), .DATA_OUT(L_A));
  Comparator #(.width(32)) comparator_1 (.a(in_8), .b(I), .gt(out_9));  // open: eq, lt
  Comparator #(.width(32), .mode("unsigned")) comparator_2 (.a(L_I), .b(L_A), .lt(out_10));  // open: gt, eq

  // Other names for the same wires on the sheet: A[31:0] = out_11; a_t[31:0] = in_6; CLOCK = in_3; I___N = out_9;
  //   i_t[31:0] = in_7; L_a_t = in_4; C = out_10; L_I____L_A = out_10; L_i_t = in_1; N[31:0] = in_8; S_a = in_5;
  //   S_i = in_2

  // Notes on the sheet:
  //   INPUT
  //   A
  //   I
  //   Data Path
  //   OUTPUT
  //   I < N
  //   L[I] < L[A]
endmodule

module CONTROL_UNIT_M (
  input  in_1,
  input  in_2,
  input  in_3,
  input  in_4,
  output out_5,
  output out_6,
  output out_7,
  output out_8,
  output out_9
);

  wire demultiplexer_1_out0, demultiplexer_2_out0, demultiplexer_2_out1, demultiplexer_3_out0,
       demultiplexer_4_out0, demultiplexer_4_out1, IDLE_q, L_A0, or_1_out, or_3_out, or_5_out, or_6_out,
       WHILE_q;

  or or_1 (or_1_out, demultiplexer_1_out0, demultiplexer_4_out1);
  D_Flip_Flop IDLE (.clk(in_2), .D(or_1_out), .Q(IDLE_q), .preset(in_4));  // open: Qn, en, reset
  Demultiplexer #(.enable("false")) demultiplexer_1 (.out0(demultiplexer_1_out0), .out1(L_A0), .in(IDLE_q), .sel(in_4));
  or or_2 (out_5, L_A0, out_7);
  or or_3 (or_3_out, L_A0, out_8);
  D_Flip_Flop WHILE (.clk(in_2), .D(or_3_out), .Q(WHILE_q));  // open: Qn, preset, en, reset
  Demultiplexer #(.enable("false")) demultiplexer_2 (
    .out0(demultiplexer_2_out0), .out1(demultiplexer_2_out1), .in(WHILE_q), .sel(in_1));
  or or_4 (out_6, L_A0, out_8);
  Demultiplexer #(.enable("false")) demultiplexer_3 (
    .out0(demultiplexer_3_out0), .out1(out_7), .in(demultiplexer_2_out1), .sel(in_3));
  or or_5 (or_5_out, demultiplexer_4_out0, demultiplexer_2_out0);
  D_Flip_Flop END (.clk(in_2), .D(or_5_out), .Q(out_9));  // open: Qn, preset, en, reset
  or or_6 (or_6_out, demultiplexer_3_out0, out_7);
  Demultiplexer #(.enable("false")) demultiplexer_4 (
    .out0(demultiplexer_4_out0), .out1(demultiplexer_4_out1), .in(out_9), .sel(in_4));
  D_Flip_Flop AFTER_IF (.clk(in_2), .D(or_6_out), .Q(out_8));  // open: Qn, preset, en, reset

  // Other names for the same wires on the sheet: CLOCK = in_2; End = out_9; I___N = in_1; L_A = out_5; L_I = out_6;
  //   L_I0 = L_A0; L_I____L_A = in_3; L_A1 = out_7; S_A = out_7; L_I1 = out_8; S_I = out_8; Start = in_4

  // Notes on the sheet:
  //   INPUT
  //   CONTROL UNIT
  //   OUTPUT
endmodule

module ASM_Min (
  input  in_1,
  input  in_2,
  input  [31:0] in_3,
  input  [31:0] in_4,
  input  [31:0] in_5,
  output OUTPUT,
  output [31:0] out_7
);

  wire control_unit_m_1_out_5, control_unit_m_1_out_6, control_unit_m_1_out_7, control_unit_m_1_out_8, I___N,
       L_I____L_A;

  CONTROL_UNIT_M control_unit_m_1 (
    .out_5(control_unit_m_1_out_5), .in_1(I___N), .out_6(control_unit_m_1_out_6),
    .out_7(control_unit_m_1_out_7), .in_3(L_I____L_A), .out_8(control_unit_m_1_out_8), .in_4(in_2),
    .out_9(OUTPUT), .in_2(in_1));
  DATA_PATH__M data_path_m_1 (
    .in_1(control_unit_m_1_out_6), .in_2(control_unit_m_1_out_8), .in_4(control_unit_m_1_out_5),
    .in_5(control_unit_m_1_out_7), .in_6(in_3), .in_7(in_5), .in_8(in_4), .out_9(I___N), .out_10(L_I____L_A),
    .out_11(out_7), .in_3(in_1));

  // Other names for the same wires on the sheet: A[31:0] = out_7; a_t[31:0] = in_3; END = OUTPUT; i[31:0] = in_4;
  //   n[31:0] = in_5; START = in_2

  // Notes on the sheet:
  //   INPUT
endmodule

module DATA_PATH (
  input  in_1,
  input  in_2,
  input  in_3,
  input  in_4,
  input  [31:0] in_5,
  input  [31:0] in_6,
  output out_7,
  output out_8,
  output [31:0] out_9,
  output [31:0] out_10
);

  wire CLOCK;
  wire [31:0] L_A, L_I, Min, Min_idx, multiplexer_1_out, V, V___1;

  Clock clock_1 (.out(CLOCK));
  Multiplexer #(.width(32), .enable("false")) multiplexer_1 (
    .in0(Min), .in1(V___1), .out(multiplexer_1_out), .sel(in_4));
  Adder #(.width(32)) adder_1 (.a(V), .b(32'h1), .out(V___1));  // open: cin, cout
  Register #(.width(32)) register_1 (.D(multiplexer_1_out), .en(in_3), .Q(V), .clk(CLOCK));  // open: clr
  ASM_Min asm_min_1 (
    .in_1(CLOCK), .in_2(1'b1), .in_3(32'h1), .in_4(32'h1), .in_5(in_6), .out_7(Min_idx));  // open: OUTPUT
  INPUT input_1 (.DIR(out_10[23:0]), .CLK(CLOCK), .DATA_OUT(L_I));
  INPUT input_2 (.DIR(out_9[23:0]), .CLK(CLOCK), .DATA_OUT(L_A));
  Comparator #(.width(32)) comparator_1 (.a(in_6), .b(out_10), .gt(out_7));  // open: eq, lt
  Comparator #(.width(32), .mode("unsigned")) comparator_2 (.a(L_I), .b(L_A), .lt(out_8));  // open: gt, eq

  // Other names for the same wires on the sheet: A[31:0] = out_9; I[31:0] = out_10; I___N = out_7; i_t[31:0] = in_5;
  //   C = out_8; L_I____L_A = out_8; L_i_t = in_1; L_v = in_3; N[31:0] = in_6; S_i = in_2; S_v = in_4

  // Notes on the sheet:
  //   INPUT
  //   Value
  //   Data Path
  //   OUTPUT
  //   I < N
  //   L[I] < L[A]
endmodule
